# Fritzing sketch fritz 3 led teransistor control (saved by Fritzing 0.9.3b)
breadboards: 1

parts:
  Part1 = Arduino Uno (Rev3)
  LED1 = LED - 5mm [color="Red (633nm)" package="5 mm [THT]"]
  Q1 = TRANSISTOR_NPN [package=to-92]
  LED2 = smd LED [color="Yellow (595nm)" package="1206 [SMD]"]
  LED3 = smd LED [color="Green (555nm)" package="1206 [SMD]"]
  Q2 = TRANSISTOR_NPN [package=to-92]
  Q3 = TRANSISTOR_NPN [package=to-92]
  J1 = Power Jack [package=power_jack_smd]

nets:
  GND: Part1.GND, Q1.C, Q2.C, Q3.C, J1.GND
  N1: Part1.D5_PWM, Q3.B
  N2: Part1.D6_PWM, Q2.B
  N3: Part1.D7, Q1.B
  N4: LED1.cathode, Q1.E
  N5: LED1.anode, LED2.anode, LED3.anode, J1.GNDBREAK
  N6: LED2.cathode, Q2.E
  N7: LED3.cathode, Q3.E
