# Fritzing sketch fritz 3 led relay control (saved by Fritzing 0.9.3b)
breadboards: 1

parts:
  Part1 = KY-019
  Part2 = Arduino Uno (Rev3)
  LED1 = LED - 5mm [color="Red (633nm)" package="5 mm [THT]"]
  LED2 = LED - 5mm [color="Yellow (595nm)" package="5 mm [THT]"]
  LED3 = LED - 5mm [color="Green (555nm)" package="5 mm [THT]"]
  Q1 = NPN-Transistor [package="TO92 [THT]"]
  Q2 = NPN-Transistor [package="TO92 [THT]"]
  Q3 = NPN-Transistor [package="TO92 [THT]"]
  Part3 = Lilypad Battery Connect
  Power_plug1 = Power plug
  LED4 = custom_light_bulb

nets:
  N1: Part1.connector0, Part2.D12/MISO
  N2: Part1.connector1, LED1.anode, LED2.anode, LED3.anode, Power_plug1.VCC
  GND: Part1.connector2, Part2.GND, Q1.C, Q2.C, Q3.C, Power_plug1.GND
  N3: Part1.connector4, Part3.-
  N4: Part1.connector5, LED4.connector0
  N5: Part2.D5_PWM, Q3.B
  N6: Part2.D6_PWM, Q2.B
  N7: Part2.D7, Q1.B
  N8: LED1.cathode, Q1.E
  N9: LED2.cathode, Q2.E
  N10: LED3.cathode, Q3.E
  N11: Part3.+, LED4.connector1
