# Fritzing sketch LEDSpush (saved by Fritzing 0.9.3b)
breadboards: 1

parts:
  S1 = Pushbutton [package="[THT]"]
  R1 = Resistor [tolerance=±5% resistance=220 package=THT]
  Part1 = Arduino Uno (Rev3)
  LED1 = LED - 3mm [color="Red (633nm)" package="3 mm [THT]"]
  R2 = Resistor [tolerance=±5% resistance=220 package=THT]

nets:
  N1: S1.Pin_1, S1.Pin_2, R1.Pin_0, Part1.D2, Part1.5V
  N2: S1.Pin_3, S1.Pin_4
  N3: R1.Pin_1, Part1.GND, LED1.cathode
  N4: Part1.D13/SCK, R2.Pin_0
  N5: LED1.anode, R2.Pin_1
