# Fritzing sketch Untitled Sketch 2 (saved by Fritzing 0.9.3b)
breadboards: 1

parts:
  مقاومت1 = Resistor [tolerance=±5% resistance=220 package=THT]
  دکمه1 = Pushbutton [package=THT]
  R1 = Resistor [tolerance=±5% resistance=220 package=THT]
  C1 = Electrolytic Capacitor [capacitance=1µF package="100 mil [THT, electrolytic]"]

nets:
  N1: مقاومت1.Pin_0, دکمه1.leg1, R1.Pin_0
  5V: مقاومت1.Pin_1
  GND: دکمه1.leg0, C1.-
  N2: R1.Pin_1, C1.+
