# Fritzing sketch Untitled Sketch 4 (saved by Fritzing 0.9.3b)
breadboards: 1

parts:
  R1 = Resistor [tolerance=±5% resistance=220 package=THT]
  دکمه = SWITCH-MOMENTARY-2 [package=tactile-pth-12mm]

nets:
  5V: R1.Pin_1
  GND: دکمه.1

notes:
  A
