# Fritzing sketch pull-down (saved by Fritzing 0.9.3b)
breadboards: 1

parts:
  مقاومت = Resistor [tolerance=±5% resistance=220 package=THT]
  دکمه = Pushbutton [package=THT]

nets:
  A: مقاومت.Pin_0, دکمه.leg1
  GND: مقاومت.Pin_1
  5V: دکمه.leg0
