# Fritzing sketch pull-up (saved by Fritzing 0.9.3b)
breadboards: 1

parts:
  مقاومت = Resistor [tolerance=±5% resistance=220 package=THT]
  دکمه = Pushbutton [package=THT]

nets:
  A: مقاومت.Pin_0, دکمه.leg1
  5V: مقاومت.Pin_1
  GND: دکمه.leg0
