# Fritzing sketch lcd (saved by Fritzing 0.9.3b)
breadboards: 1

parts:
  Part1 = Arduino Uno (Rev3)
  LCD1 = LCD screen
  R1 = Trimmer Potentiometer [maximum_resistance=10kΩ package=THT]
  R2 = Resistor [tolerance=±5% resistance=220 package=THT]

nets:
  N1: Part1.D12/MISO, LCD1.RS
  N2: Part1.D13/SCK, LCD1.E
  N3: Part1.D4, LCD1.DB4
  N4: Part1.D5_PWM, LCD1.DB5
  N5: Part1.D6_PWM, LCD1.DB6
  N6: Part1.D7, LCD1.DB7
  5V: Part1.5V, LCD1.VDD, R1.leg2, R2.Pin_0
  GND: Part1.GND, LCD1.VSS, LCD1.R/W, LCD1.LED-, R1.leg1
  N7: LCD1.V0, R1.wiper
  N8: LCD1.LED+, R2.Pin_1
